# Fritzing sketch Sterownik (saved by Fritzing 0.8.7b)
circuit board: 7.79616cm x 7.5859cm
breadboards: 1

parts:
  R1 = Resistor [tolerance=±5% resistance=220 package=THT]
  R5 = Resistor [tolerance=±5% resistance=4.7k package=THT]
  RTC1 = DS1307 RTC Breakout
  R7 = Resistor [tolerance=±5% resistance=220 package=THT]
  Arduino = Arduino Pro Mini v13
  R6 = Resistor [tolerance=±5% resistance=4.7k package=THT]

nets:
  N1: R1.Pin_0, Arduino.D2
  5V: R1.Pin_1, R5.Pin_1, RTC1.5V, R7.Pin_1, Arduino.VCC, R6.Pin_1
  N2: R5.Pin_0, RTC1.SCL, Arduino.A4
  GND: RTC1.GND, Arduino.GND
  N3: RTC1.SDA, Arduino.A5, R6.Pin_0
  N4: R7.Pin_0, Arduino.D3_PWM

notes:
  I2C
  GND

custom parts:
  DS1307 RTC Breakout: DS1307 Real-time Clock Breakout Board with Battery
